// Logisim project BigASM.circ as structural Verilog
module BOARD_BIG_ASM (
  output out_1
);

  wire button_1_out, CLK, CLR, d_ff_1_q, not_1_out, Write, Write_ASCII;
  wire [6:0] ASCII;
  wire [7:0] counter_1_q;
  wire [23:0] Dir_INPUT, Dir_MEMORY;
  wire [31:0] INPUT, MEMORY_IN, MEMORY_OUT;

  Button button_1 (.out(button_1_out));
  Clock clock_1 (.out(CLK));
  D_Flip_Flop d_ff_1 (.clk(CLK), .D(1'b1), .Q(d_ff_1_q), .reset(button_1_out));  // open: Qn, preset, en
  D_Flip_Flop d_ff_2 (.clk(CLK), .D(d_ff_1_q), .Qn(CLR), .reset(button_1_out));  // open: Q, preset, en
  BIG_ASM big_asm_1 (
    .DATA_INPUT(INPUT), .MEMORY_IN(MEMORY_OUT), .CLK(CLK), .CLR(CLR), .DIR_INPUT(Dir_INPUT),
    .MEMORY_OUT(MEMORY_IN), .DIR_MEMORY(Dir_MEMORY), .Write_OUTPUT(Write), .ASCII(ASCII),
    .Write_ASCII(Write_ASCII), .END(out_1));
  MEMORY memory_1 (.DIR(Dir_MEMORY), .DATA_IN(MEMORY_IN), .WRITE(Write), .CLK(CLK), .CLR(CLR), .DATA_OUT(MEMORY_OUT));
  INPUT input_1 (.DIR(Dir_INPUT), .CLK(CLK), .DATA_OUT(INPUT));
  Counter counter_1 (.load(1'b0), .count(not_1_out), .Q(counter_1_q), .clk(CLK), .clr(CLR));  // open: D, carry
  not not_1 (not_1_out, out_1);
  // Probe on counter_1_q
  TTY #(.rows(32), .cols(60)) tty_1 (.data(ASCII), .clk(CLK), .we(Write_ASCII), .clr(CLR));

  // Other names for the same wires on the sheet: END = out_1

  // Notes on the sheet:
  //   COUNTER
  //   BOARD
endmodule

module INPUT (
  input  [23:0] DIR,
  input  CLK,
  output [31:0] DATA_OUT
);

  RAM #(.addrWidth(24), .dataWidth(32)) ram_1 (.addr(DIR), .data(DATA_OUT), .clk(CLK), .ld(1'b1));  // open: sel, clr
endmodule

module MEMORY (
  input  [23:0] DIR,
  input  [31:0] DATA_IN,
  input  WRITE,
  input  CLK,
  input  CLR,
  output [31:0] DATA_OUT
);

  wire not_1_out;

  not not_1 (not_1_out, WRITE);
  RAM #(.addrWidth(24), .dataWidth(32), .bus("separate")) ram_1 (
    .addr(DIR), .din(DATA_IN), .data(DATA_OUT), .clk(CLK), .ld(not_1_out), .clr(CLR));  // open: str, sel
endmodule

module BIG_ASM (
  input  [31:0] DATA_INPUT,
  input  [31:0] MEMORY_IN,
  input  CLK,
  input  CLR,
  output [23:0] DIR_INPUT,
  output [31:0] MEMORY_OUT,
  output [23:0] DIR_MEMORY,
  output Write_OUTPUT,
  output [6:0] ASCII,
  output Write_ASCII,
  output END
);
endmodule

module PRINT_UDEC (
  input  [31:0] num,
  input  start,
  input  CLK,
  input  RST,
  output [6:0] ASCII,
  output Write_ASCII,
  output \end 
);

  wire _0_c, _0_n, demultiplexer_1_out0, demultiplexer_2_out0, demultiplexer_2_out1, demultiplexer_3_out0,
       demultiplexer_3_out1, IDLE_2_q, IDLE_3_q, IDLE_4_q, IDLE_q, Lc, Lc_0, Ln, Ln_0, or_1_out;
  wire [23:0] bit_extender_1_out;
  wire [31:0] c, c___1, c___1_t, divider_1_rem, memory_1_data_out, multiplexer_1_out, multiplexer_2_out,
       multiplexer_3_out, n, n___10, n___10___48;

  Multiplexer #(.width(32), .enable("false")) multiplexer_1 (
    .in0(num), .in1(n___10), .out(multiplexer_1_out), .sel(Lc_0));
  Divider #(.width(32)) divider_1 (.a(n), .b(32'ha), .out(n___10), .rem(divider_1_rem));  // open: upper
  Adder #(.width(32)) adder_1 (.a(divider_1_rem), .b(32'h30), .out(n___10___48));  // open: cin, cout
  or or_1 (or_1_out, demultiplexer_1_out0, \end );
  Register #(.width(32)) u_n (.D(multiplexer_1_out), .en(Ln), .Q(n), .clk(CLK), .clr(RST));
  D_Flip_Flop IDLE (.clk(CLK), .D(or_1_out), .Q(IDLE_q), .preset(RST));  // open: Qn, en, reset
  Demultiplexer #(.enable("false")) demultiplexer_1 (
    .out0(demultiplexer_1_out0), .out1(Ln_0), .in(IDLE_q), .sel(start));
  or or_2 (Write_ASCII, demultiplexer_3_out0, demultiplexer_2_out1);
  Multiplexer #(.width(32), .enable("false")) multiplexer_2 (
    .in0(c___1), .in1(c___1_t), .out(multiplexer_2_out), .sel(Write_ASCII));
  Adder #(.width(32)) adder_2 (.a(c), .b(32'h1), .out(c___1));  // open: cin, cout
  Subtractor #(.width(32)) subtractor_1 (.a(c), .b(32'h1), .out(c___1_t));  // open: bin, bout
  D_Flip_Flop IDLE_2 (.clk(CLK), .D(Ln_0), .Q(IDLE_2_q), .reset(RST));  // open: Qn, preset, en
  Register #(.width(32)) u_c (.D(multiplexer_2_out), .en(Lc), .Q(c), .clk(CLK), .clr(RST));
  or or_3 (Lc_0, IDLE_2_q, demultiplexer_3_out1);
  Multiplexer #(.width(32), .enable("false")) multiplexer_3 (
    .in0(c), .in1(c___1_t), .out(multiplexer_3_out), .sel(Write_ASCII));
  Comparator #(.width(32), .mode("unsigned")) comparator_1 (.a({32{1'b0}}), .b(n), .lt(_0_n));  // open: gt, eq
  Comparator #(.width(32), .mode("unsigned")) comparator_2 (.a({32{1'b0}}), .b(c), .lt(_0_c));  // open: gt, eq
  D_Flip_Flop IDLE_3 (.clk(CLK), .D(Write_ASCII), .Q(IDLE_3_q), .reset(RST));  // open: Qn, preset, en
  Demultiplexer #(.enable("false")) demultiplexer_2 (
    .out0(demultiplexer_2_out0), .out1(demultiplexer_2_out1), .in(IDLE_3_q), .sel(_0_c));
  Bit_Extender #(.in_width(32), .out_width(24)) bit_extender_1 (.in(multiplexer_3_out), .out(bit_extender_1_out));
  D_Flip_Flop IDLE_4 (.clk(CLK), .D(Lc_0), .Q(IDLE_4_q), .reset(RST));  // open: Qn, preset, en
  or or_4 (Lc, Lc_0, Write_ASCII);
  or or_5 (Ln, Ln_0, Lc_0);
  Demultiplexer #(.enable("false")) demultiplexer_3 (
    .out0(demultiplexer_3_out0), .out1(demultiplexer_3_out1), .in(IDLE_4_q), .sel(_0_n));
  D_Flip_Flop IDLE_5 (.clk(CLK), .D(demultiplexer_2_out0), .Q(\end ), .reset(RST));  // open: Qn, preset, en
  MEMORY memory_1 (
    .DIR(bit_extender_1_out), .DATA_IN(n___10___48), .WRITE(Lc_0), .CLK(CLK), .CLR(RST),
    .DATA_OUT(memory_1_data_out));
  Bit_Extender #(.in_width(32), .out_width(7)) bit_extender_2 (.in(memory_1_data_out), .out(ASCII));

  // Other names for the same wires on the sheet: Lc_1 = Write_ASCII; Sc = Write_ASCII; Ln_1 = Lc_0; Sn = Lc_0;
  //   Write = Lc_0
endmodule

module PRINT_DEC (
  input  [31:0] num,
  input  start,
  input  CLK,
  input  RST,
  output [6:0] ASCII,
  output Write_ASCII,
  output END
);

  wire demultiplexer_1_out0, demultiplexer_1_out1, demultiplexer_2_out0, demultiplexer_3_out0, end_t,
       IDLE_3_q, IDLE_q, or_1_out, or_2_out, or_3_out, S_ASCII, startUDEC, Write_ASCII_1;
  wire [6:0] ASCII_t;
  wire [31:0] multiplexer_1_out, negator_1_out;

  or or_1 (or_1_out, demultiplexer_1_out0, END);
  Negator #(.width(32)) negator_1 (.in(num), .out(negator_1_out));
  D_Flip_Flop IDLE (.clk(CLK), .D(or_1_out), .Q(IDLE_q), .preset(RST));  // open: Qn, en, reset
  Demultiplexer #(.enable("false")) demultiplexer_1 (
    .out0(demultiplexer_1_out0), .out1(demultiplexer_1_out1), .in(IDLE_q), .sel(start));
  Multiplexer #(.width(32), .enable("false")) multiplexer_1 (
    .in0(num), .in1(negator_1_out), .out(multiplexer_1_out), .sel(num[31]));
  Demultiplexer #(.enable("false")) demultiplexer_2 (
    .out0(demultiplexer_2_out0), .out1(S_ASCII), .in(demultiplexer_1_out1), .sel(num[31]));
  or or_2 (or_2_out, demultiplexer_2_out0, S_ASCII);
  D_Flip_Flop IDLE_2 (.clk(CLK), .D(or_2_out), .Q(startUDEC), .reset(RST));  // open: Qn, preset, en
  PRINT_UDEC print_udec_1 (
    .num(multiplexer_1_out), .start(startUDEC), .CLK(CLK), .RST(RST), .ASCII(ASCII_t),
    .Write_ASCII(Write_ASCII_1), .\end (end_t));
  D_Flip_Flop IDLE_3 (.clk(CLK), .D(or_3_out), .Q(IDLE_3_q), .reset(RST));  // open: Qn, preset, en
  or or_3 (or_3_out, startUDEC, demultiplexer_3_out0);
  Demultiplexer #(.enable("false")) demultiplexer_3 (
    .out0(demultiplexer_3_out0), .out1(END), .in(IDLE_3_q), .sel(end_t));
  Multiplexer #(.width(7), .enable("false")) multiplexer_2 (
    .in0(ASCII_t), .in1(7'b0101101), .out(ASCII), .sel(S_ASCII));
  or or_4 (Write_ASCII, S_ASCII, Write_ASCII_1);

  // Other names for the same wires on the sheet: sign = num[31]; Write_ASCII_0 = S_ASCII
endmodule

module TEST_PRINT (
  input  [31:0] in_1,
  output out_2
);

  wire button_1_out, button_2_out, CLK, CLR, d_ff_1_q, Write_ASCII;
  wire [6:0] ASCII;

  Button button_1 (.out(button_1_out));
  Clock clock_1 (.out(CLK));
  D_Flip_Flop d_ff_1 (.clk(CLK), .D(1'b1), .Q(d_ff_1_q), .reset(button_1_out));  // open: Qn, preset, en
  D_Flip_Flop d_ff_2 (.clk(CLK), .D(d_ff_1_q), .Qn(CLR), .reset(button_1_out));  // open: Q, preset, en
  Button button_2 (.out(button_2_out));
  PRINT_UDEC print_udec_1 ();  // open: num, start, CLK, RST, ASCII, Write_ASCII, end
  PRINT_DEC print_dec_1 (
    .num(in_1), .start(button_2_out), .CLK(CLK), .RST(CLR), .ASCII(ASCII), .Write_ASCII(Write_ASCII),
    .END(out_2));
  TTY #(.rows(32), .cols(60)) tty_1 (.data(ASCII), .clk(CLK), .we(Write_ASCII), .clr(CLR));
endmodule

module DataPath (
  input  [31:0] MOUT,
  input  [31:0] IOUT,
  input  L_temp,
  input  S_d,
  input  L_d,
  input  L_n,
  input  S_i,
  input  L_i,
  input  S_j,
  input  L_j,
  input  L_key,
  input  L_Aj,
  input  [1:0] S_Mdir,
  input  [1:0] S_MIn,
  input  S_IDir,
  input  CLK,
  output [23:0] MDIR,
  output [31:0] MIN,
  output [23:0] IDIR,
  output d__n,
  output Aj_key,
  output j__0,
  output i_n
);

  wire comparator_1_gt, comparator_3_lt;
  wire [23:0] d, d_1, d_1_t, i, i_1, i_1_t, j, j_1, j_1_t, multiplexer_1_out, multiplexer_2_out,
       multiplexer_3_out;
  wire [31:0] Aj, bit_extender_1_out, bit_extender_2_out, key, n, temp;

  Multiplexer #(.width(24)) multiplexer_1 (.in0(24'h1), .in1(d_1), .out(multiplexer_1_out), .sel(S_d));  // open: en
  Multiplexer #(.width(24)) multiplexer_2 (.in0(24'h1), .in1(i_1), .out(multiplexer_2_out), .sel(S_i));  // open: en
  Multiplexer #(.width(24)) multiplexer_3 (.in0(i_1_t), .in1(j_1_t), .out(multiplexer_3_out), .sel(S_j));  // open: en
  Register #(.width(32)) u_n (.D(IOUT), .Q(n), .clk(CLK), .clr(L_n));  // open: en
  Register #(.width(32)) u_Temp (.D(IOUT), .Q(temp), .clk(CLK), .clr(L_temp));  // open: en
  Register #(.width(24)) u_d (.D(multiplexer_1_out), .Q(d), .clk(CLK), .clr(L_d));  // open: en
  Register #(.width(24)) u_i (.D(multiplexer_2_out), .Q(i), .clk(CLK), .clr(L_i));  // open: en
  Register #(.width(24)) u_j (.D(multiplexer_3_out), .Q(j), .clk(CLK), .clr(L_j));  // open: en
  Register #(.width(32)) u_key (.D(MOUT), .Q(key), .clk(CLK), .clr(L_key));  // open: en
  Register #(.width(32)) u_Aj (.D(MOUT), .Q(Aj), .clk(CLK), .clr(L_Aj));  // open: en
  assign bit_extender_1_out = {{8{1'b0}}, d};  // Bit_Extender bit_extender_1
  assign bit_extender_2_out = {{8{1'b0}}, i};  // Bit_Extender bit_extender_2
  Adder #(.width(24)) adder_1 (.a(d), .b(24'h1), .out(d_1));  // open: cin, cout
  Subtractor #(.width(24)) subtractor_1 (.a(d), .b(24'h1), .out(d_1_t));  // open: bin, bout
  Comparator #(.width(32), .mode("unsigned")) comparator_1 (
    .a(bit_extender_1_out), .b(n), .gt(comparator_1_gt));  // open: eq, lt
  Comparator #(.width(32), .mode("unsigned")) comparator_2 (.a(Aj), .b(key), .lt(Aj_key));  // open: gt, eq
  Comparator #(.width(24), .mode("unsigned")) comparator_3 (
    .a(j), .b({24{1'b0}}), .lt(comparator_3_lt));  // open: gt, eq
  Comparator #(.width(32), .mode("unsigned")) comparator_4 (.a(bit_extender_2_out), .b(n), .lt(i_n));  // open: gt, eq
  Adder #(.width(24)) adder_2 (.a(i), .b(24'h1), .out(i_1));  // open: cin, cout
  Subtractor #(.width(24)) subtractor_2 (.a(i), .b(24'h1), .out(i_1_t));  // open: bin, bout
  Adder #(.width(24)) adder_3 (.a(j), .b(24'h1), .out(j_1));  // open: cin, cout
  Subtractor #(.width(24)) subtractor_3 (.a(j), .b(24'h1), .out(j_1_t));  // open: bin, bout
  not not_1 (d__n, comparator_1_gt);
  not not_2 (j__0, comparator_3_lt);
  Multiplexer #(.select(2), .width(24)) multiplexer_4 (
    .in0(i), .in1(j), .in2(j_1), .in3(d_1_t), .out(MDIR), .sel(S_Mdir));  // open: en
  Multiplexer #(.select(2), .width(32)) multiplexer_5 (
    .in0(temp), .in1(Aj), .in2(key), .out(MIN), .sel(S_MIn));  // open: in3, en
  Multiplexer #(.width(24)) multiplexer_6 (.in0({24{1'b0}}), .in1(d), .out(IDIR), .sel(S_IDir));  // open: en
endmodule

module Control_Unit (
  input  d__n,
  input  Aj_key,
  input  j__0,
  input  i_n,
  input  start,
  input  RST,
  input  CLK,
  output MemWrite,
  output L_temp,
  output S_d,
  output L_d,
  output L_n,
  output S_i,
  output L_i,
  output S_j,
  output L_j,
  output L_key,
  output L_Aj,
  output [1:0] S_Mdir,
  output [1:0] S_MIn,
  output S_IDir
);

  wire demultiplexer_1_out0, demultiplexer_2_out0, demultiplexer_3_out0, IDLE_2_q, L_j0, MW0, or_1_out,
       or_2_out, WHILE_3_q, WHILE_q;

  D_Flip_Flop IDLE (.clk(CLK), .reset(RST));  // open: D, Q, Qn, preset, en
  buf or_1 (or_1_out, demultiplexer_3_out0);  // OR_Gate
  D_Flip_Flop WHILE (.clk(CLK), .D(or_1_out), .Q(WHILE_q), .reset(RST));  // open: Qn, preset, en
  Demultiplexer demultiplexer_1 (.out0(demultiplexer_1_out0), .out1(L_n), .in(IDLE_2_q), .sel(start));  // open: en
  D_Flip_Flop IDLE_2 (.clk(CLK), .D(demultiplexer_1_out0), .Q(IDLE_2_q), .preset(RST));  // open: Qn, en, reset
  Demultiplexer demultiplexer_2 (.out0(demultiplexer_2_out0), .out1(L_j0), .in(WHILE_q), .sel(i_n));  // open: en
  D_Flip_Flop d_ff_1 (.clk(CLK), .D(S_IDir), .Q(L_temp), .reset(RST));  // open: Qn, preset, en
  D_Flip_Flop WHILE_2 (.clk(CLK), .D(L_j0), .reset(RST));  // open: Q, Qn, preset, en
  D_Flip_Flop WHILE_3 (.clk(CLK), .D(or_2_out), .Q(WHILE_3_q), .reset(RST));  // open: Qn, preset, en
  or or_2 (or_2_out, MW0, L_n);
  D_Flip_Flop d_ff_2 (.clk(CLK), .D(L_temp), .Q(MW0), .reset(RST));  // open: Qn, preset, en
  Demultiplexer demultiplexer_3 (.out0(demultiplexer_3_out0), .out1(S_IDir), .in(WHILE_3_q), .sel(d__n));  // open: en
  D_Flip_Flop END (.clk(CLK), .D(demultiplexer_2_out0), .reset(RST));  // open: Q, Qn, preset, en

  // Other names for the same wires on the sheet: L_d0 = L_n; L_i0 = L_n; L_key0 = L_j0; S_Mdir0[1:0] = {2{MW0}}
endmodule
